# Fritzing sketch Final (saved by Fritzing 0.9.4)
breadboards: 1

parts:
  부품1 = Arduino Uno (Rev3)
  Part1 = KY-015 Temperature & Humidity Sensor Module [package="Breakout board"]
  R1 = Photocell (LDR) [package=THT]
  R2 = Resistor [tolerance=±5% resistance=1k package=THT]

nets:
  N1: 부품1.A0, R1.pin_1, R2.Pin_0
  N2: 부품1.A1, Part1.Vin
  N3: 부품1.GND, Part1.-, R2.Pin_1
  N4: 부품1.5V, Part1.S, R1.pin_0

custom parts:
  KY-015 Temperature & Humidity Sensor Module: KY-015 temperature and humidity sensor module, provides a low-latency serial interface to measure humidity and temperature.
