# Fritzing sketch Week2 (saved by Fritzing 0.9.4)
circuit board: 8.46667cm x 5.64444cm
breadboards: 1

parts:
  부품1 = Arduino Uno (Rev3)
  LED1 = LED - 5mm [color="Red (633nm)" package="5 mm [THT]"]

nets:
  N1: 부품1.D12/MISO, LED1.anode
  N2: 부품1.GND, LED1.cathode

// code stored in the sketch: Untitled.ino
int led1 = 12;

void setup() {
  pinMode(led1, OUTPUT);
}

void loop() {
  digitalWrite(led1, HIGH);
  delay(1000);
  
  digitalWrite(led1, LOW);
  delay(1000);
}
