# Fritzing sketch DigitalButtonLED (saved by Fritzing 0.9.3b)
circuit board: 8.46667cm x 5.64444cm
breadboards: 1

parts:
  부품1 = Arduino Uno (Rev3)
  LED1 = smd LED [color="Red (633nm)" package="1206 [SMD]"]
  R1 = Resistor [tolerance=±5% resistance=10k package=THT]
  S1 = Pushbutton [package="[THT]"]

nets:
  N1: 부품1.D12/MISO, LED1.anode
  N2: 부품1.D0/RX, R1.Pin_1, S1.Pin_3, S1.Pin_4
  N3: 부품1.5V, S1.Pin_1, S1.Pin_2
  N4: 부품1.GND, LED1.cathode, R1.Pin_0
